// Logisim project COMBINATIONAL_PASSWORD_LOCK.circ as structural Verilog: 12 circuits, main circuit main
module main (
);

  wire ATTEMPT_out, CLEAR_KEYBOARD_out, CLOCK_out, controlled_buffer_1_out, ENABLE_out, keyboard_1_avail,
       sub_circuit_2_1_clock_2, sub_circuit_2_1_enable_2, sub_circuit_2_1_password_attempt_failed,
       sub_circuit_2_1_password_set, sub_circuit_2_1_password_verified;
  wire [3:0] sub_circuit_2_1_chances_left_to_verify, sub_circuit_2_1_timer;
  wire [6:0] keyboard_1_data;
  wire [27:0] sub_circuit_2_1__28_bit;

  Clock CLOCK (.out(CLOCK_out));
  Button CLEAR_KEYBOARD (.out(CLEAR_KEYBOARD_out));
  Button ENABLE (.out(ENABLE_out));
  Button ATTEMPT (.out(ATTEMPT_out));
  Hex_Digit_Display hex_digit_display_1 (.value(sub_circuit_2_1_chances_left_to_verify));  // open: dp
  Hex_Digit_Display hex_digit_display_2 (.value(sub_circuit_2_1_timer));  // open: dp
  Keyboard #(.buflen(4)) keyboard_1 (
    .clk(controlled_buffer_1_out), .clr(CLEAR_KEYBOARD_out), .avail(keyboard_1_avail), .data(keyboard_1_data));  // open: re
  assign controlled_buffer_1_out = keyboard_1_avail ? CLOCK_out : 1'bz;  // Controlled_Buffer controlled_buffer_1
  sub_circuit_2 sub_circuit_2_1 (
    .KEYBOARD(keyboard_1_data), .clock(CLOCK_out), .ENABLE(ENABLE_out), .ATTEMPT(ATTEMPT_out),
    .chances_left_to_verify(sub_circuit_2_1_chances_left_to_verify), .timer(sub_circuit_2_1_timer),
    .password_set(sub_circuit_2_1_password_set), .password_verified(sub_circuit_2_1_password_verified),
    .password_attempt_failed(sub_circuit_2_1_password_attempt_failed), ._28_bit(sub_circuit_2_1__28_bit),
    .clock_2(sub_circuit_2_1_clock_2), .enable_2(sub_circuit_2_1_enable_2));
  LED PASSWORD_HAS_BEEN_SET (.in(sub_circuit_2_1_password_set));
  LED PASSWORD_HAS_BEEN_VERIFIED (.in(sub_circuit_2_1_password_verified));
  LED PASSWORD_ATTEMPT_MADE (.in(sub_circuit_2_1_password_attempt_failed));
  TTY #(.rows(1), .cols(1)) tty_1 (
    .data(sub_circuit_2_1__28_bit[6:0]), .clk(sub_circuit_2_1_clock_2), .clr(sub_circuit_2_1_enable_2));  // open: we
  TTY #(.rows(1), .cols(1)) tty_2 (
    .data(sub_circuit_2_1__28_bit[13:7]), .clk(sub_circuit_2_1_clock_2), .clr(sub_circuit_2_1_enable_2));  // open: we
  TTY #(.rows(1), .cols(1)) tty_3 (
    .data(sub_circuit_2_1__28_bit[20:14]), .clk(sub_circuit_2_1_clock_2), .clr(sub_circuit_2_1_enable_2));  // open: we
  TTY #(.rows(1), .cols(1)) tty_4 (
    .data(sub_circuit_2_1__28_bit[27:21]), .clk(sub_circuit_2_1_clock_2), .clr(sub_circuit_2_1_enable_2));  // open: we

  // Notes on the sheet:
  //   ATTEMPTS 
  //   LEFT TO
  //   VERIFY
  //   PASSWORD
  //   PLEASE
  //   FOR
  //   WAIT
  //   TO
  //   SECONDS
  //   RESTART
  //   PLEASE ENTER HERE
  //   |
  //   |
  //   |
  //   |
  //   |
  //   |
  //   |
  //   |
  //   |
  //   |
  //   COMBINATIONAL PASSWORD CHECKER
  //   _______________________________________________________________
  //   A LOGISM SIMULATION
  //   INSTRUCTIONS :
  //   1.TO SET PASSWORD =>(PRESS ENABLE
  //   2.TO VERIFY PASSWORD=> (PRESS ATTEMPT)
  //   _______________________________________________________________________
  //   3.CIRCUIT BLOCK ATFER 3 ATTEMPTS ,WAIT FOR 9 SECONDS TO RESTART
  //   ________________________________________________________________________
  //   )
  //   VERIFIED
  //   PASSWORD
  //   DISPLAY
  //   |
  //   |
  //   |
  //   |
  //   |
  //   |
  //   |
  //   |
  //   |
endmodule

module register (
  input  [6:0] Keyboard,
  input  Enable,
  input  Clear_password,
  input  Clock,
  output [27:0] Output,
  output [2:0] Not_needed
);

  wire AND_2_out, AND_out, input_counter_1_clock_2, OR_out;
  wire [6:0] log_register_q0, log_register_q1, log_register_q2;

  Shift_Register #(.width(7), .length(4)) log_register (
    .in(Keyboard), .clk(AND_out), .clr(Clear_password), .q0(log_register_q0), .q1(log_register_q1),
    .q2(log_register_q2));  // open: shift, out, load, d0, d1, d2, d3, q3
  or OR (OR_out, Keyboard[6], Keyboard[5], Keyboard[4], Keyboard[3], Keyboard[2], Keyboard[1], Keyboard[0]);
  Register #(.width(7)) register_1 (
    .D(log_register_q2), .en(Enable), .Q(Output[6:0]), .clk(AND_out), .clr(Clear_password));
  Register #(.width(7)) register_2 (
    .D(log_register_q1), .en(Enable), .Q(Output[13:7]), .clk(AND_out), .clr(Clear_password));
  Register #(.width(7)) register_3 (
    .D(log_register_q0), .en(Enable), .Q(Output[20:14]), .clk(AND_out), .clr(Clear_password));
  Register #(.width(7)) register_4 (.D(Keyboard), .en(Enable), .Q(Output[27:21]), .clk(AND_out), .clr(Clear_password));
  and AND (AND_out, input_counter_1_clock_2, OR_out, Clock);
  DotMatrix #(.inputtype("row"), .matrixcols(7), .matrixrows(1)) dotmatrix_1 (.row0(Output[6:0]));
  DotMatrix #(.inputtype("row"), .matrixcols(7), .matrixrows(1)) dotmatrix_2 (.row0(Output[13:7]));
  DotMatrix #(.inputtype("row"), .matrixcols(7), .matrixrows(1)) dotmatrix_3 (.row0(Output[20:14]));
  DotMatrix #(.inputtype("row"), .matrixcols(7), .matrixrows(1)) dotmatrix_4 (.row0(Output[27:21]));
  and AND_2 (AND_2_out, Clock, OR_out);
  Input_counter input_counter_1 (
    .Clock(AND_2_out), .Input_5(3'b101), .Clear(Clear_password), .\output (Not_needed),
    .Clock_2(input_counter_1_clock_2));  // open: Load_not_needed, Data_in_not_needed

  // Notes on the sheet:
  //   data 1
  //   data 2
  //   data 3
  //   data 4
  //   INPUT
  //   COUNTER
endmodule

module Input_counter (
  input  Load_not_needed,
  input  [2:0] Data_in_not_needed,
  input  Clock,
  input  [2:0] Input_5,
  input  Clear,
  output [2:0] \output ,
  output Clock_2
);

  wire and_1_out, comparator_1_eq;

  and and_1 (and_1_out, Clock, Clock_2);
  Counter #(.width(3), .max('h7)) counter_1 (
    .load(Load_not_needed), .D(Data_in_not_needed), .count(1'b1), .Q(\output ), .clk(and_1_out), .clr(Clear));  // open: carry
  Comparator #(.width(3)) comparator_1 (.a(\output ), .b(Input_5), .eq(comparator_1_eq));  // open: gt, lt
  not not_1 (Clock_2, comparator_1_eq);
endmodule

module comparator (
  input  [27:0] Input_1,
  input  [27:0] Input_2,
  output Output
);

  Comparator #(.width(28)) comparator_1 (.a(Input_1), .b(Input_2), .eq(Output));  // open: gt, lt
endmodule

module _28_bit_adder (
  input  [27:0] \input ,
  output \output 
);

  wire or_1_out;

  or or_1 (or_1_out, \input [0], \input [1], \input [2], \input [3], \input [4], \input [5], \input [6], \input [7], \input [8], \input [9], \input [10], \input [11], \input [12], \input [13], \input [14], \input [15], \input [16], \input [17], \input [18], \input [19], \input [20], \input [21], \input [22], \input [23], \input [24], \input [25], \input [26]);
  or or_2 (\output , or_1_out, \input [27]);
endmodule

module sub_circuit_1 (
  input  Enable1,
  input  CLEAR_PASSWORD,
  input  [6:0] KEYBOARD,
  input  CLOCK,
  input  Enable2,
  input  CLEAR_INPUT,
  output [27:0] view_password_not_needed,
  output PASSWORD_SET,
  output PASSWORD_VERIFIED,
  output PASSWORD_ATTEMPT,
  output [27:0] view_attempt_not_needed
);

  register register_1 (
    .Keyboard(KEYBOARD), .Enable(Enable1), .Clear_password(CLEAR_PASSWORD), .Clock(CLOCK),
    .Output(view_password_not_needed));  // open: Not_needed
  register register_2 (
    .Keyboard(KEYBOARD), .Enable(Enable2), .Clear_password(CLEAR_INPUT), .Clock(CLOCK),
    .Output(view_attempt_not_needed));  // open: Not_needed
  _28_bit_adder u_28_bit_adder_1 (.\input (view_password_not_needed), .\output (PASSWORD_SET));
  comparator comparator_1 (
    .Input_1(view_password_not_needed), .Input_2(view_attempt_not_needed), .Output(PASSWORD_VERIFIED));
  _28_bit_adder u_28_bit_adder_2 (.\input (view_attempt_not_needed), .\output (PASSWORD_ATTEMPT));

  // Notes on the sheet:
  //   REGISTER
  //   REGISTER
  //   28 BIT ADDER
  //   COMPARATOR
  //   28 BIT ADDER
endmodule

module sub_circuit_2 (
  input  [6:0] KEYBOARD,
  input  clock,
  input  ENABLE,
  input  ATTEMPT,
  output password_set,
  output password_verified,
  output password_attempt_failed,
  output [27:0] _28_bit,
  output clock_2,
  output enable_2,
  output [3:0] chances_left_to_verify,
  output [3:0] timer
);

  wire AND_out, comparator_1_eq, enable_1_output, n9_to_0_counter_1_out_5, not_1_out, OR_2_out, OR_out,
       rectify_1_enable_input, sub_circuit_1_1_password_verified, XNOR_out;
  wire [2:0] input_counter_1_output;

  rectify rectify_1 (.ENABLE(ENABLE), .chances_input(chances_left_to_verify), .enable_input(rectify_1_enable_input));
  enable enable_1 (.enable(rectify_1_enable_input), .ATTEMPT(ATTEMPT), .OUTPUT(enable_1_output));
  Chances_counter chances_counter_1 (.Input({1'b0, input_counter_1_output}), .Output(chances_left_to_verify));
  xnor XNOR (XNOR_out, comparator_1_eq, enable_1_output);
  sub_circuit_1 sub_circuit_1_1 (
    .Enable1(enable_1_output), .CLEAR_PASSWORD(rectify_1_enable_input), .KEYBOARD(KEYBOARD), .CLOCK(clock),
    .Enable2(XNOR_out), .CLEAR_INPUT(OR_out), .PASSWORD_SET(password_set),
    .PASSWORD_VERIFIED(sub_circuit_1_1_password_verified), .PASSWORD_ATTEMPT(password_attempt_failed),
    .view_attempt_not_needed(_28_bit));  // open: view_password_not_needed
  or OR (OR_out, rectify_1_enable_input, ATTEMPT);
  not not_1 (not_1_out, sub_circuit_1_1_password_verified);
  and AND (AND_out, not_1_out, ATTEMPT);
  or OR_2 (OR_2_out, sub_circuit_1_1_password_verified, n9_to_0_counter_1_out_5);
  Input_counter input_counter_1 (
    .Clock(AND_out), .Input_5(3'b100), .Clear(OR_2_out), .\output (input_counter_1_output));  // open: Load_not_needed, Data_in_not_needed, Clock_2
  and and_2 (clock_2, password_set, sub_circuit_1_1_password_verified);
  Comparator #(.width(3)) comparator_1 (.a(input_counter_1_output), .b(3'b100), .eq(comparator_1_eq));  // open: gt, lt
  or OR_3 (enable_2, rectify_1_enable_input, ATTEMPT);
  _9_to_0_counter u_9_to_0_counter_1 (
    .Clock(clock), .Start(comparator_1_eq), .Reset(n9_to_0_counter_1_out_5), .Output(timer),
    .out_5(n9_to_0_counter_1_out_5));

  assign password_verified = clock_2;

  // Notes on the sheet:
  //   ENABLE
  //   CHANCES
  //   COUNTER
  //   SUB
  //   CIRCUIT 1
  //   INPUT
  //   COUNTER
  //   CMP
  //   9 T0 0
  //   COUNTER
endmodule

module _9_to_0_counter (
  input  Clock,
  input  Start,
  input  Reset,
  output [3:0] Output,
  output out_5
);

  wire and_1_out, comparator_1_gt, comparator_1_lt, or_1_out;
  wire [3:0] counter_1_q;

  Counter #(.width(4), .max('hf)) counter_1 (
    .count(1'b1), .Q(counter_1_q), .clk(and_1_out), .clr(Reset));  // open: load, D, carry
  and and_1 (and_1_out, Clock, Start, or_1_out);
  Subtractor #(.width(4)) subtractor_1 (.a(4'b1001), .b(counter_1_q), .out(Output));  // open: bin, bout
  Comparator #(.width(4)) comparator_1 (
    .a(4'b1001), .b(counter_1_q), .gt(comparator_1_gt), .lt(comparator_1_lt));  // open: eq
  or or_1 (or_1_out, comparator_1_gt, comparator_1_lt);
  not not_1 (out_5, or_1_out);
endmodule

module Chances_counter (
  input  [3:0] Input,
  output [3:0] Output
);

  Subtractor #(.width(4)) subtractor_1 (.a(4'b0011), .b(Input), .out(Output));  // open: bin, bout
endmodule

module enable (
  input  enable,
  input  ATTEMPT,
  output OUTPUT
);

  D_Flip_Flop d_ff_1 (.clk(enable), .D(1'b1), .Q(OUTPUT), .reset(ATTEMPT));  // open: Qn, preset, en
endmodule

module rectify (
  input  ENABLE,
  input  [3:0] chances_input,
  output enable_input
);

  wire comparator_1_eq;
  wire [3:0] and_1_out;
  wire [3:3] not_1_out;

  Comparator #(.width(4)) comparator_1 (.a(chances_input), .b(4'b1111), .eq(comparator_1_eq));  // open: gt, lt
  not not_1 (not_1_out[3], comparator_1_eq);
  assign and_1_out = {4{ENABLE}} & {4{not_1_out[3]}};  // AND_Gate and_1, 4 bits wide
  or or_1 (enable_input, and_1_out[0], and_1_out[1], and_1_out[2], and_1_out[3]);
endmodule

module reset (
  input  reset,
  input  set_change_password,
  input  remove_password,
  input  ATTEMPT,
  input  [3:0] chances_input,
  output set_password,
  output remove_password_2
);

  wire d_ff_1_q, rectify_1_enable_input;

  rectify rectify_1 (.ENABLE(reset), .chances_input(chances_input), .enable_input(rectify_1_enable_input));
  D_Flip_Flop d_ff_1 (.clk(rectify_1_enable_input), .Q(d_ff_1_q), .reset(ATTEMPT));  // open: D, Qn, preset, en
  D_Flip_Flop d_ff_2 (
    .clk(set_change_password), .D(d_ff_1_q), .Q(set_password), .reset(ATTEMPT));  // open: Qn, preset, en
  D_Flip_Flop d_ff_3 (
    .clk(remove_password), .D(d_ff_1_q), .Q(remove_password_2), .reset(ATTEMPT));  // open: Qn, preset, en
endmodule
